# Fritzing sketch arduino_prog_hvpp (saved by Fritzing 0.7.12b)

parts:
  Arduino1 = Arduino
  U1 = 74HC595 [package="DIP16 [THT]"]
  C1 = Electrolytic Capacitor [capacitance=0.1µF package="100 mil [THT, electrolytic]"]

nets:
  GND: Arduino1.GND, U1.GND, U1.OE, C1.-
  N1: Arduino1.D13, U1.SH_CP
  N2: Arduino1.D11, U1.DS
  +5V: Arduino1.+5V, U1.MR, U1.VCC, C1.+
  N3: Arduino1.A1, U1.ST_CP

notes:
  CTRL0
  CTRL2
  CTRL3
  CTRL4
  CTRL5
  CTRL6
  CTRL7
  D7:0
  HVRESET
  SVCC
  RDY
  XTAL
