# Fritzing sketch arduino_prog_hvsp (saved by Fritzing 0.7.12b)

parts:
  Arduino1 = Arduino
  C1 = Electrolytic Capacitor [capacitance=1µF package="100 mil [THT, electrolytic]"]  # not connected

nets:
  RESET: Arduino1.D10

notes:
  GND
  SVCC
  HVRESET
  SDI
  SDO
  SCI
  SII
