# Fritzing sketch arduino_prog_isp (saved by Fritzing 0.7.12b)

parts:
  Arduino1 = Arduino
  C1 = Electrolytic Capacitor [capacitance=1µF package="100 mil [THT, electrolytic]"]

nets:
  RESET: Arduino1.D10
  N1: Arduino1.RST, C1.+
  N2: Arduino1.GND, C1.-

notes:
  GND
  VCC
  RESET
  MOSI
  MISO
  SCK
  XTAL
